# Fritzing sketch servoControlPanel (saved by Fritzing 0.9.3b)
breadboards: 1

parts:
  Sign_Switch = Pushbutton [package="[THT]"]
  Zero_Switch_Pulldown = Resistor [tolerance=±5% resistance=10k package=THT]
  Autosweep_Switch_Pulldown = Resistor [tolerance=±5% resistance=10k package=THT]
  Servo_Angle_Knob = Trimmer Potentiometer [maximum_resistance=10kΩ package=THT]
  Autosweep_ON/OFF_Switch = Pushbutton [package="[THT]"]
  Zero_Switch = Pushbutton [package="[THT]"]
  R1 = Resistor [tolerance=±5% resistance=220 package=THT]
  Servo_Knob_Capacitor = Electrolytic Capacitor [capacitance=100µF package="100 mil [THT, electrolytic]"]
  Sign_Switch_Pulldown = Resistor [tolerance=±5% resistance=10k package=THT]
  Arduino_UNO = Arduino Uno (Rev3)
  Servo = Basic Servo
  LCD = LCD screen
  LCD_Contrast_Knob = Trimmer Potentiometer [maximum_resistance=10kΩ package=THT]
  Servo_Capacitor = Electrolytic Capacitor [capacitance=100µF package="100 mil [THT, electrolytic]"]

nets:
  5V: Sign_Switch.Pin_1, Sign_Switch.Pin_2, Servo_Angle_Knob.leg1, Autosweep_ON/OFF_Switch.Pin_1, Autosweep_ON/OFF_Switch.Pin_2, Zero_Switch.Pin_1, Zero_Switch.Pin_2, R1.Pin_0, Servo_Knob_Capacitor.+, Arduino_UNO.5V, Servo.vcc, LCD.VDD, LCD_Contrast_Knob.leg1, Servo_Capacitor.+
  N1: Sign_Switch.Pin_3, Sign_Switch.Pin_4, Sign_Switch_Pulldown.Pin_0, Arduino_UNO.D6_PWM
  N2: Zero_Switch_Pulldown.Pin_0, Zero_Switch.Pin_3, Zero_Switch.Pin_4, Arduino_UNO.D8
  GND: Zero_Switch_Pulldown.Pin_1, Autosweep_Switch_Pulldown.Pin_1, Servo_Angle_Knob.leg2, Servo_Knob_Capacitor.-, Sign_Switch_Pulldown.Pin_1, Arduino_UNO.GND, Servo.gnd, LCD.VSS, LCD.R/W, LCD.LED-, LCD_Contrast_Knob.leg2, Servo_Capacitor.-
  N3: Autosweep_Switch_Pulldown.Pin_0, Autosweep_ON/OFF_Switch.Pin_3, Autosweep_ON/OFF_Switch.Pin_4, Arduino_UNO.D7
  N4: Servo_Angle_Knob.wiper, Arduino_UNO.A0
  N5: R1.Pin_1, LCD.LED+
  N6: Arduino_UNO.D9_PWM, Servo.pulse
  N7: Arduino_UNO.D11_PWM/MOSI, LCD.E
  N8: Arduino_UNO.D12/MISO, LCD.RS
  N9: Arduino_UNO.D2, LCD.DB7
  N10: Arduino_UNO.D3_PWM, LCD.DB6
  N11: Arduino_UNO.D4, LCD.DB5
  N12: Arduino_UNO.D5_PWM, LCD.DB4
  N13: LCD.V0, LCD_Contrast_Knob.wiper
